# Fritzing sketch HC-05 Accel Wiring (saved by Fritzing 0.9.3b)
breadboards: 1

parts:
  Part1 = Arduino Uno (Rev3)
  GY1 = MPU-6050 Board GY-521 [form="♀ (female)" package=THT]
  HC-05 = Bluetooth HC-05 Macho

nets:
  N1: Part1.A4/SDA, GY1.pin4
  N2: Part1.A5/SCL, GY1.pin3
  N3: Part1.D10_PWM/SS, HC-05.TXD
  N4: Part1.D11_PWM/MOSI, HC-05.RXD
  N5: Part1.D12/MISO, HC-05.Key
  N6: Part1.D2, GY1.pin8
  5V: Part1.5V, GY1.pin1, HC-05.VCC
  GND: Part1.GND, GY1.pin2, GY1.pin7, HC-05.GND

custom parts:
  MPU-6050 Board GY-521: Acelerometro y Giroscopio MPU-6050 Board GY-521
